// Logisim project Experiment_1_regular(by_GGN).circ as structural Verilog: 8 circuits, main circuit main
module main (
);

  wire button_1_out, clock_1_out, controller_1_alusrc, controller_1_extop, controller_1_memtoreg,
       controller_1_memwrite, controller_1_npc_sel, controller_1_regdst, controller_1_regwrite,
       controller_1_swap, not_1_out, or_1_out;
  wire [1:0] controller_1_aluop;
  wire [4:0] ifu_1_instr, ifu_1_instr_2, ifu_1_instr_4, multiplexer_1_out;
  wire [5:0] ifu_1_instr_5;
  wire [10:0] ifu_1_instr_3;
  wire [31:0] alu_1_c, dm_1_memout, ext_1_b, gpr_1_rd1, gpr_1_rd2, multiplexer_2_out, multiplexer_3_out;

  Clock clock_1 (.out(clock_1_out));
  Button button_1 (.out(button_1_out));
  // Probe on {ifu_1_instr_5, ifu_1_instr_2, ifu_1_instr, ifu_1_instr_4, ifu_1_instr_3}
  IFU ifu_1 (
    .IfBeq(controller_1_npc_sel), .Zero(not_1_out), .Clk(clock_1_out), .Reset(button_1_out),
    .Instr({ifu_1_instr_5, ifu_1_instr_2, ifu_1_instr, ifu_1_instr_4, ifu_1_instr_3}));
  Multiplexer #(.width(5)) multiplexer_1 (
    .in0(ifu_1_instr), .in1(ifu_1_instr_4), .out(multiplexer_1_out), .sel(controller_1_regdst));
  Controller controller_1 (
    .op(ifu_1_instr_5), .func(ifu_1_instr_3[5:0]), .Aluop(controller_1_aluop), .extop(controller_1_extop),
    .npc_sel(controller_1_npc_sel), .Regdst(controller_1_regdst), .Memtoreg(controller_1_memtoreg),
    .Memwrite(controller_1_memwrite), .Alusrc(controller_1_alusrc), .Regwrite(controller_1_regwrite),
    .swap(controller_1_swap));
  GPR gpr_1 (
    .Wd(multiplexer_3_out), .clk(clock_1_out), .Reset(button_1_out), .A3(multiplexer_1_out),
    .A1(ifu_1_instr_2), .A2(ifu_1_instr), .Regwrite(controller_1_regwrite), .Rd1(gpr_1_rd1), .Rd2(gpr_1_rd2));
  // Probe on multiplexer_2_out
  // Probe on gpr_1_rd1
  Multiplexer #(.width(32)) multiplexer_2 (
    .in0(gpr_1_rd2), .in1(ext_1_b), .out(multiplexer_2_out), .sel(controller_1_alusrc));
  Ext ext_1 (.A({ifu_1_instr_4, ifu_1_instr_3}), .Extop(controller_1_extop), .swap(controller_1_swap), .B(ext_1_b));
  Multiplexer #(.width(32)) multiplexer_3 (
    .in0(alu_1_c), .in1(dm_1_memout), .out(multiplexer_3_out), .sel(controller_1_memtoreg));
  not not_1 (not_1_out, or_1_out);
  or or_1 (or_1_out, 1'b0, alu_1_c[0], alu_1_c[1], alu_1_c[2], alu_1_c[3], alu_1_c[4], alu_1_c[5], alu_1_c[6], alu_1_c[7], alu_1_c[8], alu_1_c[9], alu_1_c[10], alu_1_c[11], alu_1_c[12], alu_1_c[13], alu_1_c[14], alu_1_c[15], alu_1_c[16], alu_1_c[17], alu_1_c[18], alu_1_c[19], alu_1_c[20], alu_1_c[21], alu_1_c[22], alu_1_c[23], alu_1_c[24], alu_1_c[25], alu_1_c[26], alu_1_c[27], alu_1_c[28], alu_1_c[29], alu_1_c[30], alu_1_c[31]);
  // Probe on alu_1_c
  ALU alu_1 (.F(controller_1_aluop), .A(gpr_1_rd1), .B(multiplexer_2_out), .C0(1'b0), .C(alu_1_c));
  DM dm_1 (
    .A(alu_1_c[4:0]), .Memwrite(controller_1_memwrite), .Memtoreg(controller_1_memtoreg), .Clk(clock_1_out),
    .D(gpr_1_rd2), .Reset(button_1_out), .MEMout(dm_1_memout));
endmodule

module GPR (
  input  [31:0] Wd,
  input  clk,
  input  Reset,
  input  [4:0] A3,
  input  [4:0] A1,
  input  [4:0] A2,
  input  Regwrite,
  output [31:0] Rd1,
  output [31:0] Rd2
);

  wire decoder_1_out0, decoder_1_out1, decoder_1_out2, decoder_1_out3, decoder_1_out4, decoder_1_out5,
       decoder_1_out6, decoder_1_out7, decoder_1_out8, decoder_1_out9, decoder_1_out10, decoder_1_out11,
       decoder_1_out12, decoder_1_out13, decoder_1_out14, decoder_1_out17, decoder_1_out18, decoder_1_out19,
       decoder_1_out20, decoder_1_out21, decoder_1_out22, decoder_1_out23, decoder_1_out24, decoder_1_out25,
       decoder_1_out26, decoder_1_out27, decoder_1_out28, decoder_1_out29, decoder_1_out30, decoder_1_out31,
       W_R15, W_R16;
  wire [31:0] register_1_q, register_2_q, register_3_q, register_4_q, register_5_q, register_6_q,
       register_7_q, register_8_q, register_9_q, register_10_q, register_11_q, register_12_q, register_13_q,
       register_14_q, register_15_q, register_16_q, register_17_q, register_18_q, register_19_q,
       register_20_q, register_21_q, register_22_q, register_23_q, register_24_q, register_25_q,
       register_26_q, register_27_q, register_28_q, register_29_q, register_30_q, register_31_q,
       register_32_q;

  Decoder #(.select(5)) decoder_1 (
    .out0(decoder_1_out0), .out1(decoder_1_out1), .out2(decoder_1_out2), .out3(decoder_1_out3),
    .out4(decoder_1_out4), .out5(decoder_1_out5), .out6(decoder_1_out6), .out7(decoder_1_out7),
    .out8(decoder_1_out8), .out9(decoder_1_out9), .out10(decoder_1_out10), .out11(decoder_1_out11),
    .out12(decoder_1_out12), .out13(decoder_1_out13), .out14(decoder_1_out14), .out15(W_R15), .out16(W_R16),
    .out17(decoder_1_out17), .out18(decoder_1_out18), .out19(decoder_1_out19), .out20(decoder_1_out20),
    .out21(decoder_1_out21), .out22(decoder_1_out22), .out23(decoder_1_out23), .out24(decoder_1_out24),
    .out25(decoder_1_out25), .out26(decoder_1_out26), .out27(decoder_1_out27), .out28(decoder_1_out28),
    .out29(decoder_1_out29), .out30(decoder_1_out30), .out31(decoder_1_out31), .sel(A3), .en(Regwrite));
  Register #(.width(32)) register_1 (.D(Wd), .en(decoder_1_out17), .clk(clk), .Q(register_1_q), .clr(Reset));
  Register #(.width(32)) register_2 (.D(Wd), .en(decoder_1_out18), .clk(clk), .Q(register_2_q));  // open: clr
  Register #(.width(32)) register_3 (.D(Wd), .en(decoder_1_out19), .clk(clk), .Q(register_3_q), .clr(Reset));
  Register #(.width(32)) register_4 (.D(Wd), .en(decoder_1_out20), .clk(clk), .Q(register_4_q), .clr(Reset));
  Register #(.width(32)) register_5 (.D(Wd), .en(decoder_1_out21), .clk(clk), .Q(register_5_q), .clr(Reset));
  Register #(.width(32)) register_6 (.D(Wd), .en(decoder_1_out22), .clk(clk), .Q(register_6_q), .clr(Reset));
  Register #(.width(32)) register_7 (.D(Wd), .en(decoder_1_out23), .clk(clk), .Q(register_7_q), .clr(Reset));
  Register #(.width(32)) register_8 (.D(Wd), .en(decoder_1_out24), .clk(clk), .Q(register_8_q), .clr(Reset));
  Register #(.width(32)) register_9 (.D(Wd), .en(decoder_1_out25), .clk(clk), .Q(register_9_q), .clr(Reset));
  Register #(.width(32)) register_10 (.D(Wd), .en(decoder_1_out26), .clk(clk), .Q(register_10_q), .clr(Reset));
  Register #(.width(32)) register_11 (.D(Wd), .en(decoder_1_out27), .clk(clk), .Q(register_11_q), .clr(Reset));
  Register #(.width(32)) register_12 (.D(Wd), .en(decoder_1_out28), .clk(clk), .Q(register_12_q), .clr(Reset));
  Register #(.width(32)) register_13 (.D(Wd), .en(decoder_1_out29), .clk(clk), .Q(register_13_q), .clr(Reset));
  Register #(.width(32)) register_14 (.D(Wd), .en(decoder_1_out30), .clk(clk), .Q(register_14_q), .clr(Reset));
  Register #(.width(32)) register_15 (.D(Wd), .en(decoder_1_out31), .clk(clk), .Q(register_15_q), .clr(Reset));
  Register #(.width(32)) register_16 (.D(Wd), .en(decoder_1_out0), .clk(clk), .Q(register_16_q), .clr(Reset));
  Register #(.width(32)) register_17 (.D(Wd), .en(decoder_1_out1), .clk(clk), .Q(register_17_q), .clr(Reset));
  Register #(.width(32)) register_18 (.D(Wd), .en(decoder_1_out2), .clk(clk), .Q(register_18_q), .clr(Reset));
  Register #(.width(32)) register_19 (.D(Wd), .en(decoder_1_out3), .clk(clk), .Q(register_19_q), .clr(Reset));
  Register #(.width(32)) register_20 (.D(Wd), .en(decoder_1_out4), .clk(clk), .Q(register_20_q), .clr(Reset));
  Register #(.width(32)) register_21 (.D(Wd), .en(decoder_1_out5), .clk(clk), .Q(register_21_q), .clr(Reset));
  Register #(.width(32)) register_22 (.D(Wd), .en(decoder_1_out6), .clk(clk), .Q(register_22_q), .clr(Reset));
  Register #(.width(32)) register_23 (.D(Wd), .en(decoder_1_out7), .clk(clk), .Q(register_23_q), .clr(Reset));
  Register #(.width(32)) register_24 (.D(Wd), .en(decoder_1_out8), .clk(clk), .Q(register_24_q), .clr(Reset));
  Register #(.width(32)) register_25 (.D(Wd), .en(decoder_1_out9), .clk(clk), .Q(register_25_q), .clr(Reset));
  Register #(.width(32)) register_26 (.D(Wd), .en(decoder_1_out10), .clk(clk), .Q(register_26_q), .clr(Reset));
  Register #(.width(32)) register_27 (.D(Wd), .en(decoder_1_out11), .clk(clk), .Q(register_27_q), .clr(Reset));
  Register #(.width(32)) register_28 (.D(Wd), .en(decoder_1_out12), .clk(clk), .Q(register_28_q), .clr(Reset));
  Register #(.width(32)) register_29 (.D(Wd), .en(decoder_1_out13), .clk(clk), .Q(register_29_q), .clr(Reset));
  Register #(.width(32)) register_30 (.D(Wd), .en(decoder_1_out14), .clk(clk), .Q(register_30_q), .clr(Reset));
  Register #(.width(32)) register_31 (.D(Wd), .en(W_R15), .clk(clk), .Q(register_31_q), .clr(Reset));
  Register #(.width(32)) register_32 (.D(Wd), .en(W_R16), .clk(clk), .Q(register_32_q), .clr(Reset));
  Multiplexer #(.select(5), .width(32)) multiplexer_1 (
    .in0(register_16_q), .in1(register_17_q), .in2(register_18_q), .in3(register_19_q), .in4(register_20_q),
    .in5(register_21_q), .in6(register_22_q), .in7(register_23_q), .in8(register_24_q), .in9(register_25_q),
    .in10(register_26_q), .in11(register_27_q), .in12(register_28_q), .in13(register_29_q),
    .in14(register_30_q), .in15(register_31_q), .in16(register_32_q), .in17(register_1_q),
    .in18(register_2_q), .in19(register_3_q), .in20(register_4_q), .in21(register_5_q), .in22(register_6_q),
    .in23(register_7_q), .in24(register_8_q), .in25(register_9_q), .in26(register_10_q),
    .in27(register_11_q), .in28(register_12_q), .in29(register_13_q), .in30(register_14_q),
    .in31(register_15_q), .out(Rd1), .sel(A1));
  Multiplexer #(.select(5), .width(32)) multiplexer_2 (
    .in0(register_16_q), .in1(register_17_q), .in2(register_18_q), .in3(register_19_q), .in4(register_20_q),
    .in5(register_21_q), .in6(register_22_q), .in7(register_23_q), .in8(register_24_q), .in9(register_25_q),
    .in10(register_26_q), .in11(register_27_q), .in12(register_28_q), .in13(register_29_q),
    .in14(register_30_q), .in15(register_31_q), .in16(register_32_q), .in17(register_1_q),
    .in18(register_2_q), .in19(register_3_q), .in20(register_4_q), .in21(register_5_q), .in22(register_6_q),
    .in23(register_7_q), .in24(register_8_q), .in25(register_9_q), .in26(register_10_q),
    .in27(register_11_q), .in28(register_12_q), .in29(register_13_q), .in30(register_14_q),
    .in31(register_15_q), .out(Rd2), .sel(A2));
endmodule

module ALU (
  input  [1:0] F,
  input  [31:0] A,
  input  [31:0] B,
  input  C0,
  output [31:0] C
);

  wire myadder_1_c1, myadder_2_c1, myadder_3_c1, myadder_4_c1, myadder_5_c1, myadder_6_c1, myadder_7_c1,
       myadder_8_c1, myadder_9_c1, myadder_10_c1, myadder_11_c1, myadder_12_c1, myadder_13_c1, myadder_14_c1,
       myadder_15_c1, myadder_16_c1, myadder_17_c1, myadder_18_c1, myadder_19_c1, myadder_20_c1,
       myadder_21_c1, myadder_22_c1, myadder_23_c1, myadder_24_c1, myadder_25_c1, myadder_26_c1,
       myadder_27_c1, myadder_28_c1, myadder_29_c1, myadder_30_c1, myadder_31_c1, not_2_out, or_2_out;
  wire [31:0] ALUor, ALUsum, multiplexer_1_out, not_1_out;

  assign not_1_out = ~B;  // NOT_Gate not_1, 32 bits wide
  Multiplexer #(.width(32)) multiplexer_1 (.in0(not_1_out), .in1(B), .out(multiplexer_1_out), .sel(F[0]));
  assign ALUor = A | B;  // OR_Gate or_1, 32 bits wide
  not not_2 (not_2_out, F[0]);
  or or_2 (or_2_out, not_2_out, C0);
  Multiplexer #(.width(32)) multiplexer_2 (.in0(ALUor), .in1(ALUsum), .out(C), .sel(F[1]));
  MyAdder myadder_1 (.A(A[0]), .B(multiplexer_1_out[0]), .C0(or_2_out), .X(ALUsum[0]), .C1(myadder_1_c1));
  MyAdder myadder_2 (.A(A[1]), .B(multiplexer_1_out[1]), .C0(myadder_1_c1), .X(ALUsum[1]), .C1(myadder_2_c1));
  MyAdder myadder_3 (.A(A[2]), .B(multiplexer_1_out[2]), .C0(myadder_2_c1), .X(ALUsum[2]), .C1(myadder_3_c1));
  MyAdder myadder_4 (.A(A[3]), .B(multiplexer_1_out[3]), .C0(myadder_3_c1), .X(ALUsum[3]), .C1(myadder_4_c1));
  MyAdder myadder_5 (.A(A[4]), .B(multiplexer_1_out[4]), .C0(myadder_4_c1), .X(ALUsum[4]), .C1(myadder_5_c1));
  MyAdder myadder_6 (.A(A[5]), .B(multiplexer_1_out[5]), .C0(myadder_5_c1), .X(ALUsum[5]), .C1(myadder_6_c1));
  MyAdder myadder_7 (.A(A[6]), .B(multiplexer_1_out[6]), .C0(myadder_6_c1), .X(ALUsum[6]), .C1(myadder_7_c1));
  MyAdder myadder_8 (.A(A[7]), .B(multiplexer_1_out[7]), .C0(myadder_7_c1), .X(ALUsum[7]), .C1(myadder_8_c1));
  MyAdder myadder_9 (.A(A[8]), .B(multiplexer_1_out[8]), .C0(myadder_8_c1), .X(ALUsum[8]), .C1(myadder_9_c1));
  MyAdder myadder_10 (.A(A[9]), .B(multiplexer_1_out[9]), .C0(myadder_9_c1), .X(ALUsum[9]), .C1(myadder_10_c1));
  MyAdder myadder_11 (.A(A[10]), .B(multiplexer_1_out[10]), .C0(myadder_10_c1), .X(ALUsum[10]), .C1(myadder_11_c1));
  MyAdder myadder_12 (.A(A[11]), .B(multiplexer_1_out[11]), .C0(myadder_11_c1), .X(ALUsum[11]), .C1(myadder_12_c1));
  MyAdder myadder_13 (.A(A[12]), .B(multiplexer_1_out[12]), .C0(myadder_12_c1), .X(ALUsum[12]), .C1(myadder_13_c1));
  MyAdder myadder_14 (.A(A[13]), .B(multiplexer_1_out[13]), .C0(myadder_13_c1), .X(ALUsum[13]), .C1(myadder_14_c1));
  MyAdder myadder_15 (.A(A[14]), .B(multiplexer_1_out[14]), .C0(myadder_14_c1), .X(ALUsum[14]), .C1(myadder_15_c1));
  MyAdder myadder_16 (.A(A[15]), .B(multiplexer_1_out[15]), .C0(myadder_15_c1), .X(ALUsum[15]), .C1(myadder_16_c1));
  MyAdder myadder_17 (.A(A[16]), .B(multiplexer_1_out[16]), .C0(myadder_16_c1), .X(ALUsum[16]), .C1(myadder_17_c1));
  MyAdder myadder_18 (.A(A[17]), .B(multiplexer_1_out[17]), .C0(myadder_17_c1), .X(ALUsum[17]), .C1(myadder_18_c1));
  MyAdder myadder_19 (.A(A[18]), .B(multiplexer_1_out[18]), .C0(myadder_18_c1), .X(ALUsum[18]), .C1(myadder_19_c1));
  MyAdder myadder_20 (.A(A[19]), .B(multiplexer_1_out[19]), .C0(myadder_19_c1), .X(ALUsum[19]), .C1(myadder_20_c1));
  MyAdder myadder_21 (.A(A[20]), .B(multiplexer_1_out[20]), .C0(myadder_20_c1), .X(ALUsum[20]), .C1(myadder_21_c1));
  MyAdder myadder_22 (.A(A[21]), .B(multiplexer_1_out[21]), .C0(myadder_21_c1), .X(ALUsum[21]), .C1(myadder_22_c1));
  MyAdder myadder_23 (.A(A[22]), .B(multiplexer_1_out[22]), .C0(myadder_22_c1), .X(ALUsum[22]), .C1(myadder_23_c1));
  MyAdder myadder_24 (.A(A[23]), .B(multiplexer_1_out[23]), .C0(myadder_23_c1), .X(ALUsum[23]), .C1(myadder_24_c1));
  MyAdder myadder_25 (.A(A[24]), .B(multiplexer_1_out[24]), .C0(myadder_24_c1), .X(ALUsum[24]), .C1(myadder_25_c1));
  MyAdder myadder_26 (.A(A[25]), .B(multiplexer_1_out[25]), .C0(myadder_25_c1), .X(ALUsum[25]), .C1(myadder_26_c1));
  MyAdder myadder_27 (.A(A[26]), .B(multiplexer_1_out[26]), .C0(myadder_26_c1), .X(ALUsum[26]), .C1(myadder_27_c1));
  MyAdder myadder_28 (.A(A[27]), .B(multiplexer_1_out[27]), .C0(myadder_27_c1), .X(ALUsum[27]), .C1(myadder_28_c1));
  MyAdder myadder_29 (.A(A[28]), .B(multiplexer_1_out[28]), .C0(myadder_28_c1), .X(ALUsum[28]), .C1(myadder_29_c1));
  MyAdder myadder_30 (.A(A[29]), .B(multiplexer_1_out[29]), .C0(myadder_29_c1), .X(ALUsum[29]), .C1(myadder_30_c1));
  MyAdder myadder_31 (.A(A[30]), .B(multiplexer_1_out[30]), .C0(myadder_30_c1), .X(ALUsum[30]), .C1(myadder_31_c1));
  MyAdder myadder_32 (.A(A[31]), .B(multiplexer_1_out[31]), .C0(myadder_31_c1), .X(ALUsum[31]));  // open: C1
endmodule

module MyAdder (
  input  A,
  input  B,
  input  C0,
  output X,
  output C1
);

  wire and_1_out, and_2_out, and_3_out, xor_1_out;

  xor xor_1 (xor_1_out, A, B);
  and and_1 (and_1_out, A, B);
  and and_2 (and_2_out, A, C0);
  and and_3 (and_3_out, B, C0);
  xor xor_2 (X, xor_1_out, C0);
  or or_1 (C1, and_1_out, and_2_out, and_3_out);
endmodule

module IFU (
  input  IfBeq,
  input  Zero,
  input  Clk,
  input  Reset,
  output [31:0] Instr
);

  wire and_1_out;
  wire [31:0] alu_1_c, bit_extender_1_out, multiplexer_1_out, PC_q;

  ALU alu_1 (.F(2'b11), .A(PC_q), .B(multiplexer_1_out), .C0(1'b1), .C(alu_1_c));
  Register #(.width(32)) PC (.D(alu_1_c), .en(1'b1), .clk(Clk), .Q(PC_q), .clr(Reset));
  ROM #(.addrWidth(5), .dataWidth(32)) IM (.addr(PC_q[4:0]), .data(Instr));
  and and_1 (and_1_out, IfBeq, Zero);
  Multiplexer #(.width(32)) multiplexer_1 (
    .in0({32{1'b0}}), .in1(bit_extender_1_out), .out(multiplexer_1_out), .sel(and_1_out));
  assign bit_extender_1_out = {{16{Instr[15]}}, Instr[15:0]};  // Bit_Extender bit_extender_1

  // Notes on the sheet:
  //   contents of IM (hex, n*v repeats v):
  //   3c090000 35290001 3c0a0000 36b300c1 3c0b0000 356b0000 3c0c0000 358c0001 112a0003 1695821 1894821
  //   1000fffc ac0b0007
endmodule

module Ext (
  input  [15:0] A,
  input  Extop,
  input  swap,
  output [31:0] B
);

  wire [31:0] bit_extender_1_out, bit_extender_2_out, multiplexer_1_out;

  assign bit_extender_1_out = {{16{1'b0}}, A};  // Bit_Extender bit_extender_1
  assign bit_extender_2_out = {{16{A[15]}}, A};  // Bit_Extender bit_extender_2
  Multiplexer #(.width(32)) multiplexer_1 (
    .in0(bit_extender_1_out), .in1(bit_extender_2_out), .out(multiplexer_1_out), .sel(Extop));
  Multiplexer #(.width(32)) multiplexer_2 (
    .in0(multiplexer_1_out), .in1({multiplexer_1_out[15:0], multiplexer_1_out[31:16]}), .out(B), .sel(swap));
endmodule

module DM (
  input  [4:0] A,
  input  Memwrite,
  input  Memtoreg,
  input  Clk,
  input  [31:0] D,
  input  Reset,
  output [31:0] MEMout
);

  RAM #(.addrWidth(5), .asyncread("true"), .dataWidth(32)) ram_1 (
    .addr(A), .we(Memwrite), .oe(Memtoreg), .clk(Clk), .din(D), .dout(MEMout));
endmodule

module Controller (
  input  [5:0] op,
  input  [5:0] func,
  output [1:0] Aluop,
  output extop,
  output npc_sel,
  output Regdst,
  output Memtoreg,
  output Memwrite,
  output Alusrc,
  output Regwrite,
  output swap
);

  wire ADDU_out, not_1_out, not_2_out, not_3_out, not_4_out, not_5_out, not_6_out, not_7_out, not_8_out,
       not_9_out, not_10_out, not_11_out, not_12_out, ORI_out, Special_out, SUBU_out;

  not not_1 (not_1_out, op[5]);
  not not_2 (not_2_out, op[4]);
  not not_3 (not_3_out, op[3]);
  not not_4 (not_4_out, op[2]);
  not not_5 (not_5_out, op[1]);
  not not_6 (not_6_out, op[0]);
  and Special (Special_out, not_1_out, not_2_out, not_3_out, not_4_out, not_5_out, not_6_out);
  and ORI (ORI_out, not_1_out, not_2_out, op[3], op[2], not_5_out, op[0]);
  and LW (Memtoreg, op[5], not_2_out, not_3_out, not_4_out, op[1], op[0]);
  and SW (Memwrite, op[5], not_2_out, op[3], not_4_out, op[1], op[0]);
  and BEQ (npc_sel, not_1_out, not_2_out, not_3_out, op[2], not_5_out, not_6_out);
  and LUI (swap, not_1_out, not_2_out, op[3], op[2], op[1], op[0]);
  not not_7 (not_7_out, func[5]);
  not not_8 (not_8_out, func[4]);
  not not_9 (not_9_out, func[3]);
  not not_10 (not_10_out, func[2]);
  not not_11 (not_11_out, func[1]);
  not not_12 (not_12_out, func[0]);
  and ADDU (ADDU_out, func[5], not_8_out, not_9_out, not_10_out, not_11_out, func[0], Special_out);
  and SUBU (SUBU_out, func[5], not_8_out, not_9_out, not_10_out, func[1], func[0], Special_out);
  or or_1 (Aluop[1], SUBU_out, Memtoreg, npc_sel, Memwrite, ADDU_out);
  or or_2 (Aluop[0], ORI_out, Memtoreg, Memwrite, ADDU_out);
  or or_3 (extop, Memtoreg, Memwrite);
  or or_4 (Regdst, ADDU_out, SUBU_out);
  or or_5 (Alusrc, ORI_out, Memtoreg, swap, Memwrite);
  or or_6 (Regwrite, ADDU_out, SUBU_out, ORI_out, Memtoreg, swap);
endmodule
