// Logisim project my_singlecycleprocessor.circ as structural Verilog: 11 circuits, main circuit add4
module main (
);

  wire button_1_out, clock_1_out, controller_1_alusrc, controller_1_extop, controller_1_memtoreg,
       controller_1_memwrite, controller_1_npc_sel, controller_1_regdst, controller_1_regwrite,
       controller_1_swap, nor_1_out;
  wire [1:0] controller_1_aluop;
  wire [4:0] multiplexer_1_out;
  wire [31:0] alu_1_c, dm_1_memout, ext_1_b, gpr_1_rd1, gpr_1_rd2, ifu_1_instr, multiplexer_2_out,
       multiplexer_3_out;

  Clock clock_1 (.out(clock_1_out));
  Button button_1 (.out(button_1_out));
  // Probe on ifu_1_instr
  IFU ifu_1 (
    .IfBeq(controller_1_npc_sel), .Clk(clock_1_out), .Reset(button_1_out), .Zero(nor_1_out),
    .Instr(ifu_1_instr));
  Multiplexer #(.width(5)) multiplexer_1 (
    .in0(ifu_1_instr[20:16]), .in1(ifu_1_instr[15:11]), .out(multiplexer_1_out), .sel(controller_1_regdst));
  Controller controller_1 (
    .op(ifu_1_instr[31:26]), .func(ifu_1_instr[5:0]), .Aluop(controller_1_aluop), .extop(controller_1_extop),
    .npc_sel(controller_1_npc_sel), .Regdst(controller_1_regdst), .Memtoreg(controller_1_memtoreg),
    .Memwrite(controller_1_memwrite), .Alusrc(controller_1_alusrc), .Regwrite(controller_1_regwrite),
    .swap(controller_1_swap));
  GPR gpr_1 (
    .Regwrite(controller_1_regwrite), .A3(multiplexer_1_out), .A1(ifu_1_instr[25:21]),
    .A2(ifu_1_instr[20:16]), .Wd(multiplexer_3_out), .reset(button_1_out), .clk(clock_1_out),
    .Rd1(gpr_1_rd1), .Rd2(gpr_1_rd2));
  Multiplexer #(.width(32)) multiplexer_2 (
    .in0(gpr_1_rd2), .in1(ext_1_b), .out(multiplexer_2_out), .sel(controller_1_alusrc));
  EXT ext_1 (.A(ifu_1_instr[15:0]), .swap(controller_1_swap), .Extop(controller_1_extop), .B(ext_1_b));
  Multiplexer #(.width(32)) multiplexer_3 (
    .in0(alu_1_c), .in1(dm_1_memout), .out(multiplexer_3_out), .sel(controller_1_memtoreg));
  // Probe on gpr_1_rd1
  // Probe on multiplexer_2_out
  nor nor_1 (nor_1_out, 1'b0, alu_1_c[0], alu_1_c[1], alu_1_c[2], alu_1_c[3], alu_1_c[4], alu_1_c[5], alu_1_c[6], alu_1_c[7], alu_1_c[8], alu_1_c[9], alu_1_c[10], alu_1_c[11], alu_1_c[12], alu_1_c[13], alu_1_c[14], alu_1_c[15], alu_1_c[16], alu_1_c[17], alu_1_c[18], alu_1_c[19], alu_1_c[20], alu_1_c[21], alu_1_c[22], alu_1_c[23], alu_1_c[24], alu_1_c[25], alu_1_c[26], alu_1_c[27], alu_1_c[28], alu_1_c[29], alu_1_c[30], alu_1_c[31]);
  // Probe on alu_1_c
  ALU alu_1 (.F(controller_1_aluop), .A(gpr_1_rd1), .B(multiplexer_2_out), .C(alu_1_c));
  DM dm_1 (
    .A(alu_1_c[4:0]), .Memwrite(controller_1_memwrite), .Memtoreg(controller_1_memtoreg), .Clk(clock_1_out),
    .D(gpr_1_rd2), .Reset(button_1_out), .MEMout(dm_1_memout));
endmodule

module add4 (
  input  C0,
  input  A4,
  input  B4,
  input  A3,
  input  B3,
  input  A2,
  input  B2,
  input  A1,
  input  B1,
  output G,
  output P,
  output S4,
  output S3,
  output S2,
  output S1
);

  wire and_1_out, and_2_out, and_3_out, and_4_out, and_6_out, and_7_out, and_8_out, and_9_out, and_10_out,
       and_11_out, and_12_out, and_13_out, and_14_out, or_2_out, or_3_out, or_4_out, xor_1_out, xor_3_out,
       xor_5_out, xor_7_out;

  and and_1 (and_1_out, xor_1_out, and_6_out);
  or or_1 (G, and_4_out, and_1_out, and_2_out, and_3_out);
  and and_2 (and_2_out, xor_1_out, xor_3_out, and_10_out);
  and and_3 (and_3_out, xor_1_out, xor_3_out, xor_5_out, and_13_out);
  and and_4 (and_4_out, A4, B4);
  xor xor_1 (xor_1_out, A4, B4);
  and and_5 (P, xor_1_out, xor_3_out, xor_5_out, xor_7_out, C0);
  xor xor_2 (S4, xor_1_out, or_2_out);
  and and_6 (and_6_out, A3, B3);
  or or_2 (or_2_out, and_6_out, and_7_out, and_8_out, and_9_out);
  and and_7 (and_7_out, xor_3_out, and_10_out);
  and and_8 (and_8_out, xor_3_out, xor_5_out, and_13_out);
  xor xor_3 (xor_3_out, A3, B3);
  and and_9 (and_9_out, xor_3_out, xor_5_out, xor_7_out, C0);
  xor xor_4 (S3, xor_3_out, or_3_out);
  xor xor_5 (xor_5_out, A2, B2);
  and and_10 (and_10_out, A2, B2);
  or or_3 (or_3_out, and_10_out, and_11_out, and_12_out);
  and and_11 (and_11_out, xor_5_out, and_13_out);
  and and_12 (and_12_out, xor_5_out, xor_7_out, C0);
  xor xor_6 (S2, xor_5_out, or_4_out);
  or or_4 (or_4_out, and_13_out, and_14_out);
  and and_13 (and_13_out, A1, B1);
  and and_14 (and_14_out, xor_7_out, C0);
  xor xor_7 (xor_7_out, A1, B1);
  xor xor_8 (S1, xor_7_out, C0);
endmodule

module add16 (
  input  C0,
  input  [15:0] A,
  input  [15:0] B,
  output C16,
  output [15:0] S
);

  wire add4_1_g, add4_1_p, add4_2_g, add4_2_p, add4_3_g, add4_3_p, add4_4_g, add4_4_p, and_1_out, and_2_out,
       and_3_out, and_4_out, and_5_out, and_6_out, and_7_out, and_8_out, and_9_out, nand_2_out, nor_1_out,
       or_1_out, or_2_out, or_3_out;

  and and_1 (and_1_out, add4_1_p, add4_2_g);
  nor nor_1 (nor_1_out, add4_1_g, and_1_out, and_2_out, and_3_out);
  and and_2 (and_2_out, add4_1_p, add4_2_p, add4_3_g);
  and and_3 (and_3_out, add4_1_p, add4_2_p, add4_3_p, add4_4_g);
  add4 add4_1 (
    .C0(or_1_out), .A4(A[15]), .B4(B[15]), .A3(A[14]), .B3(B[14]), .A2(A[13]), .B2(B[13]), .A1(A[12]),
    .B1(B[12]), .G(add4_1_g), .P(add4_1_p), .S4(S[15]), .S3(S[14]), .S2(S[13]), .S1(S[12]));
  nand nand_1 (C16, nor_1_out, nand_2_out);
  nand nand_2 (nand_2_out, add4_1_p, add4_2_p, add4_3_p, add4_4_p, C0);
  add4 add4_2 (
    .C0(or_2_out), .A4(A[11]), .B4(B[11]), .A3(A[10]), .B3(B[10]), .A2(A[9]), .B2(B[9]), .A1(A[8]),
    .B1(B[8]), .G(add4_2_g), .P(add4_2_p), .S4(S[11]), .S3(S[10]), .S2(S[9]), .S1(S[8]));
  or or_1 (or_1_out, add4_2_g, and_4_out, and_5_out, and_6_out);
  and and_4 (and_4_out, add4_2_p, add4_3_g);
  and and_5 (and_5_out, add4_2_p, add4_3_p, add4_4_g);
  and and_6 (and_6_out, add4_2_p, add4_3_p, add4_4_p, C0);
  add4 add4_3 (
    .C0(or_3_out), .A4(A[7]), .B4(B[7]), .A3(A[6]), .B3(B[6]), .A2(A[5]), .B2(B[5]), .A1(A[4]), .B1(B[4]),
    .G(add4_3_g), .P(add4_3_p), .S4(S[7]), .S3(S[6]), .S2(S[5]), .S1(S[4]));
  or or_2 (or_2_out, add4_3_g, and_7_out, and_8_out);
  and and_7 (and_7_out, add4_3_p, add4_4_g);
  and and_8 (and_8_out, add4_3_p, add4_4_p, C0);
  or or_3 (or_3_out, add4_4_g, and_9_out);
  and and_9 (and_9_out, add4_4_p, C0);
  add4 add4_4 (
    .C0(C0), .A4(A[3]), .B4(B[3]), .A3(A[2]), .B3(B[2]), .A2(A[1]), .B2(B[1]), .A1(A[0]), .B1(B[0]),
    .G(add4_4_g), .P(add4_4_p), .S4(S[3]), .S3(S[2]), .S2(S[1]), .S1(S[0]));
endmodule

module add32 (
  input  C0,
  input  [31:0] B,
  input  [31:0] A,
  output [31:0] out_4
);

  wire add16_2_c16;

  add16 add16_1 (.C0(add16_2_c16), .A(A[31:16]), .B(B[31:16]), .S(out_4[31:16]));  // open: C16
  add16 add16_2 (.C0(C0), .A(A[15:0]), .B(B[15:0]), .C16(add16_2_c16), .S(out_4[15:0]));
endmodule

module or32 (
  input  [31:0] A,
  input  [31:0] B,
  output [31:0] out_3
);

  assign out_3 = A | B;  // OR_Gate or_1, 32 bits wide
endmodule

module ALU (
  input  [1:0] F,
  input  [31:0] A,
  input  [31:0] B,
  output [31:0] C
);

  wire not_1_out;
  wire [31:0] add32_1_out_4, multiplexer_1_out, not_2_out, or32_1_out_3;

  not not_1 (not_1_out, F[0]);
  assign not_2_out = ~B;  // NOT_Gate not_2, 32 bits wide
  Multiplexer #(.width(32)) multiplexer_1 (.in0(not_2_out), .in1(B), .out(multiplexer_1_out), .sel(F[0]));
  or32 or32_1 (.A(A), .B(B), .out_3(or32_1_out_3));
  add32 add32_1 (.C0(not_1_out), .B(A), .A(multiplexer_1_out), .out_4(add32_1_out_4));
  Multiplexer #(.width(32)) multiplexer_2 (.in0(or32_1_out_3), .in1(add32_1_out_4), .out(C), .sel(F[1]));
endmodule

module GPR (
  input  Regwrite,
  input  [4:0] A3,
  input  [4:0] A1,
  input  [4:0] A2,
  input  [31:0] Wd,
  input  reset,
  input  clk,
  output [31:0] Rd1,
  output [31:0] Rd2
);

  wire WR0, WR1, WR2, WR3, WR4, WR5, WR6, WR7, WR8, WR9, WR10, WR11, WR12, WR13, WR14, WR15, WR16, WR17,
       WR18, WR19, WR20, WR21, WR22, WR23, WR24, WR25, WR26, WR27, WR28, WR29, WR30, WR31;
  wire [31:0] RD0, RD1_t, RD2_t, RD3, RD4, RD5, RD6, RD7, RD8, RD9, RD10, RD11, RD12, RD13, RD14, RD15, RD16,
       RD17, RD18, RD19, RD20, RD21, RD22, RD23, RD24, RD25, RD26, RD27, RD28, RD29, RD30, RD31;

  Decoder #(.select(5)) decoder_1 (
    .out0(WR0), .out1(WR1), .out2(WR2), .out3(WR3), .out4(WR4), .out5(WR5), .out6(WR6), .out7(WR7),
    .out8(WR8), .out9(WR9), .out10(WR10), .out11(WR11), .out12(WR12), .out13(WR13), .out14(WR14),
    .out15(WR15), .out16(WR16), .out17(WR17), .out18(WR18), .out19(WR19), .out20(WR20), .out21(WR21),
    .out22(WR22), .out23(WR23), .out24(WR24), .out25(WR25), .out26(WR26), .out27(WR27), .out28(WR12),
    .out29(WR13), .out30(WR14), .out31(WR15), .sel(A3), .en(Regwrite));
  Register #(.width(32)) register_1 (.D(Wd), .en(WR0), .clk(clk), .Q(RD0), .clr(reset));
  Register #(.width(32)) register_2 (.D(Wd), .en(WR1), .clk(clk), .Q(RD1_t), .clr(reset));
  Register #(.width(32)) register_3 (.D(Wd), .en(WR2), .clk(clk), .Q(RD2_t), .clr(reset));
  Register #(.width(32)) register_4 (.D(Wd), .en(WR3), .clk(clk), .Q(RD3), .clr(reset));
  Register #(.width(32)) register_5 (.D(Wd), .en(WR4), .clk(clk), .Q(RD4), .clr(reset));
  Register #(.width(32)) register_6 (.D(Wd), .en(WR5), .clk(clk), .Q(RD5), .clr(reset));
  Register #(.width(32)) register_7 (.D(Wd), .en(WR6), .clk(clk), .Q(RD6), .clr(reset));
  Register #(.width(32)) register_8 (.D(Wd), .en(WR7), .clk(clk), .Q(RD7), .clr(reset));
  Register #(.width(32)) register_9 (.D(Wd), .en(WR8), .clk(clk), .Q(RD8), .clr(reset));
  Register #(.width(32)) register_10 (.D(Wd), .en(WR9), .clk(clk), .Q(RD9), .clr(reset));
  Register #(.width(32)) register_11 (.D(Wd), .en(WR10), .clk(clk), .Q(RD10), .clr(reset));
  Register #(.width(32)) register_12 (.D(Wd), .en(WR11), .clk(clk), .Q(RD11), .clr(reset));
  Register #(.width(32)) register_13 (.D(Wd), .en(WR12), .clk(clk), .Q(RD12), .clr(reset));
  Register #(.width(32)) register_14 (.D(Wd), .en(WR13), .clk(clk), .Q(RD13), .clr(reset));
  Register #(.width(32)) register_15 (.D(Wd), .en(WR14), .clk(clk), .Q(RD14), .clr(reset));
  Register #(.width(32)) register_16 (.D(Wd), .en(WR15), .clk(clk), .Q(RD15), .clr(reset));
  Multiplexer #(.select(5), .width(32)) multiplexer_1 (
    .in0(RD0), .in1(RD1_t), .in2(RD2_t), .in3(RD3), .in4(RD4), .in5(RD5), .in6(RD6), .in7(RD7), .in8(RD8),
    .in9(RD9), .in10(RD10), .in11(RD11), .in12(RD12), .in13(RD13), .in14(RD14), .in15(RD15), .in16(RD16),
    .in17(RD17), .in18(RD18), .in19(RD19), .in20(RD20), .in21(RD21), .in22(RD22), .in23(RD23), .in24(RD24),
    .in25(RD25), .in26(RD26), .in27(RD27), .in28(RD28), .in29(RD29), .in30(RD30), .in31(RD31), .out(Rd1),
    .sel(A1));
  Register #(.width(32)) register_17 (.D(Wd), .en(WR16), .clk(clk), .Q(RD16), .clr(reset));
  Register #(.width(32)) register_18 (.D(Wd), .en(WR17), .clk(clk), .Q(RD17), .clr(reset));
  Register #(.width(32)) register_19 (.D(Wd), .en(WR18), .clk(clk), .Q(RD18), .clr(reset));
  Register #(.width(32)) register_20 (.D(Wd), .en(WR19), .clk(clk), .Q(RD19), .clr(reset));
  Register #(.width(32)) register_21 (.D(Wd), .en(WR20), .clk(clk), .Q(RD20), .clr(reset));
  Register #(.width(32)) register_22 (.D(Wd), .en(WR21), .clk(clk), .Q(RD21), .clr(reset));
  Register #(.width(32)) register_23 (.D(Wd), .en(WR22), .clk(clk), .Q(RD22), .clr(reset));
  Register #(.width(32)) register_24 (.D(Wd), .en(WR23), .clk(clk), .Q(RD23), .clr(reset));
  Register #(.width(32)) register_25 (.D(Wd), .en(WR24), .clk(clk), .Q(RD24), .clr(reset));
  Register #(.width(32)) register_26 (.D(Wd), .en(WR25), .clk(clk), .Q(RD25), .clr(reset));
  Register #(.width(32)) register_27 (.D(Wd), .en(WR26), .clk(clk), .Q(RD26), .clr(reset));
  Register #(.width(32)) register_28 (.D(Wd), .en(WR27), .clk(clk), .Q(RD27), .clr(reset));
  Register #(.width(32)) register_29 (.D(Wd), .en(WR28), .clk(clk), .Q(RD28), .clr(reset));
  Register #(.width(32)) register_30 (.D(Wd), .en(WR29), .clk(clk), .Q(RD29), .clr(reset));
  Register #(.width(32)) register_31 (.D(Wd), .en(WR30), .clk(clk), .Q(RD30), .clr(reset));
  Register #(.width(32)) register_32 (.D(Wd), .en(WR31), .clk(clk), .Q(RD31), .clr(reset));
  Multiplexer #(.select(5), .width(32)) multiplexer_2 (
    .in0(RD0), .in1(RD1_t), .in2(RD2_t), .in3(RD3), .in4(RD4), .in5(RD5), .in6(RD6), .in7(RD7), .in8(RD8),
    .in9(RD9), .in10(RD10), .in11(RD11), .in12(RD12), .in13(RD13), .in14(RD14), .in15(RD15), .in16(RD16),
    .in17(RD17), .in18(RD18), .in19(RD19), .in20(RD20), .in21(RD21), .in22(RD22), .in23(RD23), .in24(RD24),
    .in25(RD25), .in26(RD26), .in27(RD27), .in28(RD28), .in29(RD29), .in30(RD30), .in31(RD31), .out(Rd2),
    .sel(A2));
endmodule

module EXT (
  input  [15:0] A,
  input  swap,
  input  Extop,
  output [31:0] B
);

  wire [31:0] bit_extender_1_out, bit_extender_2_out, multiplexer_1_out;

  assign bit_extender_1_out = {{16{1'b0}}, A};  // Bit_Extender bit_extender_1
  assign bit_extender_2_out = {{16{A[15]}}, A};  // Bit_Extender bit_extender_2
  Multiplexer #(.width(32)) multiplexer_1 (
    .in0(bit_extender_1_out), .in1(bit_extender_2_out), .out(multiplexer_1_out), .sel(Extop));
  Multiplexer #(.width(32)) multiplexer_2 (
    .in0(multiplexer_1_out), .in1({multiplexer_1_out[15:0], multiplexer_1_out[31:16]}), .out(B), .sel(swap));
endmodule

module DM (
  input  [4:0] A,
  input  Memwrite,
  input  Memtoreg,
  input  Clk,
  input  [31:0] D,
  input  Reset,
  output [31:0] MEMout
);

  RAM #(.addrWidth(5), .asyncread("true"), .dataWidth(32)) ram_1 (
    .addr(A), .we(Memwrite), .oe(Memtoreg), .clk(Clk), .din(D), .dout(MEMout));
endmodule

module IFU (
  input  IfBeq,
  input  Clk,
  input  Reset,
  input  Zero,
  output [31:0] Instr
);

  wire and_1_out;
  wire [31:0] alu_1_c, alu_2_c, bit_extender_1_out, multiplexer_1_out, PC_q;

  Register #(.width(32)) PC (.D(alu_1_c), .en(1'b1), .clk(Clk), .Q(PC_q), .clr(Reset));
  ALU alu_1 (.F(2'b11), .A(PC_q), .B(alu_2_c), .C(alu_1_c));
  ROM #(.addrWidth(5), .dataWidth(32)) rom_1 (.addr(PC_q[4:0]), .data(Instr));
  and and_1 (and_1_out, IfBeq, Zero);
  assign bit_extender_1_out = {{16{Instr[15]}}, Instr[15:0]};  // Bit_Extender bit_extender_1
  Multiplexer #(.width(32)) multiplexer_1 (
    .in0({32{1'b0}}), .in1(bit_extender_1_out), .out(multiplexer_1_out), .sel(and_1_out));
  ALU alu_2 (.F(2'b11), .A(multiplexer_1_out), .B(32'h1), .C(alu_2_c));

  // Notes on the sheet:
  //   contents of rom_1 (hex, n*v repeats v):
  //   8d55000f 8ee40014 952821 36b300c1 ae450003 2755823 8dc2000b 104b0002 0 0 3c0d0457 1a50821
endmodule

module Controller (
  input  [5:0] op,
  input  [5:0] func,
  output [1:0] Aluop,
  output extop,
  output npc_sel,
  output Regdst,
  output Memtoreg,
  output Memwrite,
  output Alusrc,
  output Regwrite,
  output swap
);

  wire ADDU_out, not_1_out, not_2_out, not_3_out, not_4_out, not_5_out, not_6_out, not_7_out, not_8_out,
       not_9_out, not_10_out, ORI_out, Special_out, SUBU_out;

  not not_1 (not_1_out, op[5]);
  not not_2 (not_2_out, op[4]);
  not not_3 (not_3_out, op[3]);
  not not_4 (not_4_out, op[2]);
  not not_5 (not_5_out, op[1]);
  not not_6 (not_6_out, op[0]);
  and Special (Special_out, not_1_out, not_2_out, not_3_out, not_4_out, not_5_out, not_6_out);
  and ORI (ORI_out, not_1_out, not_2_out, op[3], op[2], not_5_out, op[0]);
  and LW (Memtoreg, op[5], not_2_out, not_3_out, not_4_out, op[1], op[0]);
  and SW (Memwrite, op[5], not_2_out, op[3], not_4_out, op[1], op[0]);
  and BEQ (npc_sel, not_1_out, not_2_out, not_3_out, op[2], not_5_out, not_6_out);
  and LUI (swap, not_1_out, not_2_out, op[3], op[2], op[1], op[0]);
  not not_7 (not_7_out, func[4]);
  not not_8 (not_8_out, func[3]);
  not not_9 (not_9_out, func[2]);
  not not_10 (not_10_out, func[1]);
  and ADDU (ADDU_out, func[5], not_7_out, not_8_out, not_9_out, not_10_out, func[0], Special_out);
  and SUBU (SUBU_out, func[5], not_7_out, not_8_out, not_9_out, func[1], func[0], Special_out);
  or or_1 (Aluop[1], SUBU_out, Memtoreg, npc_sel, Memwrite, ADDU_out);
  or or_2 (Aluop[0], ORI_out, Memtoreg, Memwrite, ADDU_out);
  or or_3 (extop, Memtoreg, Memwrite);
  or or_4 (Regdst, ADDU_out, SUBU_out);
  or or_5 (Alusrc, ORI_out, Memtoreg, swap, Memwrite);
  or or_6 (Regwrite, ADDU_out, SUBU_out, ORI_out, Memtoreg, swap);
endmodule
